// Logisim project MIPS.circ as structural Verilog: 1 circuit, main circuit main
module main (
  input  RegDst,
  input  ALUSrc,
  input  RegWrite,
  input  MemWrite,
  input  MemtoReg,
  input  [2:0] ALUControl
);

  wire button_1_out, CLK;
  wire [4:0] multiplexer_1_out, rom_1_data_2;
  wire [7:0] adder_1_out, PC_q;
  wire [31:0] alu_1_alu_result, bit_extender_1_out, data_mem_1_rd, multiplexer_2_out, multiplexer_3_out,
       regfile32_1_rd1, regfile32_1_rd2, rom_1_data;

  Clock clock_1 (.out(CLK));
  Button button_1 (.out(button_1_out));
  Register PC (.D(adder_1_out), .Q(PC_q), .clk(CLK), .clr(button_1_out));  // open: en
  Adder adder_1 (.a(PC_q), .b(8'h4), .out(adder_1_out));  // open: cin, cout
  // Probe on rom_1_data_2
  ROM #(.addrWidth(6), .dataWidth(32)) rom_1 (
    .addr(PC_q[7:2]), .data({rom_1_data[31:26], rom_1_data_2, rom_1_data[20:0]}));  // open: sel
  assign bit_extender_1_out = {{16{rom_1_data[15]}}, rom_1_data[15:0]};  // Bit_Extender bit_extender_1
  RegFile32 regfile32_1 (
    .AD1(rom_1_data_2), .AD2(rom_1_data[20:16]), .CLK(CLK), .WE(RegWrite), .AD3(multiplexer_1_out),
    .WD3(multiplexer_3_out), .RD1(regfile32_1_rd1), .RD2(regfile32_1_rd2));
  Multiplexer #(.width(5)) multiplexer_1 (
    .in0(rom_1_data[20:16]), .in1(rom_1_data[15:11]), .out(multiplexer_1_out), .sel(RegDst));  // open: en
  Multiplexer #(.width(32)) multiplexer_2 (
    .in0(regfile32_1_rd2), .in1(bit_extender_1_out), .out(multiplexer_2_out), .sel(ALUSrc));  // open: en
  ALU alu_1 (
    .SrcA(regfile32_1_rd1), .SrcB(multiplexer_2_out), .ALU_Control(ALUControl), .ALU_Result(alu_1_alu_result));  // open: Zero
  Data_Mem data_mem_1 (.A(alu_1_alu_result), .CLK(CLK), .WE(MemWrite), .WD(regfile32_1_rd2), .RD(data_mem_1_rd));
  Multiplexer #(.width(32)) multiplexer_3 (
    .in0(alu_1_alu_result), .in1(data_mem_1_rd), .out(multiplexer_3_out), .sel(MemtoReg));  // open: en

  // Notes on the sheet:
  //   A AND NOT B : 100
  //   A OR NOT B : 101
  //   AND : 000
  //   OR : 001
  //   + : 010
  //   A - B : 110
  //   SLT : 111
  //   add t2, t1, t0
  //   lw t0 0x00(zero)
  //   sw t0 0x01(zero)
  //   lw t1 0x02(zero)
  //   contents of rom_1 (hex, n*v repeats v):
  //   8c080000 ac080001 8c090002 1285020
endmodule
